# Fritzing sketch Wiring diagram (saved by Fritzing 0.9.4)
breadboards: 1

parts:
  ZS-042_RTC1 = ZS-042 RTC Module
  5V_LED = LED - 5mm [color="Red (633nm)" package="5 mm [THT]"]
  GND = single row smd female pin header, 1 pin [form="♀ (female)"]
  3v3 = female pin header, 1 pin [form="♀ (female)"]
  SCL = female pin header, 1 pin [form="♀ (female)"]
  5V = female pin header, 1 pin [form="♀ (female)"]
  SDA = female pin header, 1 pin [form="♀ (female)"]
  5V_Buzzer = Buzzer 12mm [package=buzzer-ccv]
  GND_2 = female pin header, 1 pin [form="♀ (female)"]
  Line_2 = female pin header, 1 pin [form="♀ (female)"]
  Q3 = NPN-Transistor [package="TO92 [THT]"]
  Q4 = NPN-Transistor [package="TO92 [THT]"]
  Line_1 = female pin header, 1 pin [form="♀ (female)"]
  R1 = Resistor [tolerance=±5% resistance=100k package="0402 [SMD]"]
  R2 = Resistor [tolerance=±5% resistance=100k package="0402 [SMD]"]

nets:
  N1: ZS-042_RTC1.GND, GND.pin1
  N2: ZS-042_RTC1.VCC, 3v3.pin1
  N3: ZS-042_RTC1.SDA, SDA.pin1
  N4: ZS-042_RTC1.SCL, SCL.pin1
  N5: 5V_LED.cathode, Q3.E
  N6: 5V_LED.anode, 5V.pin1, 5V_Buzzer.2
  N7: 5V_Buzzer.1, Q4.E
  N8: GND_2.pin1, Q3.C, Q4.C
  N9: Line_2.pin1, R1.Pin_1
  N10: Q3.B, R2.Pin_0
  N11: Q4.B, R1.Pin_0
  N12: Line_1.pin1, R2.Pin_1
